# Fritzing sketch client schematic (saved by Fritzing 0.7.11b)

parts:
  R1 = Resistor [tolerance=±5% resistance=220 package="0805 [SMD]"]
  R2 = Resistor [tolerance=±5% resistance=220 package="0805 [SMD]"]
  LED1 = LED - 5mm [color="Red (633nm)" package="5 mm [THT]"]
  LED2 = green LED - 5mm [package="5 mm [THT]"]
  Part1 = Arduino Wireless SD Shield
  U1 = XBee

nets:
  N1: R1.Pin_0, Part1.N$64
  N2: R1.Pin_1, Part1.D7, Part1.N$60
  N3: R2.Pin_0, Part1.N$171
  N4: R2.Pin_1, Part1.D6, Part1.N$169
  GND: LED1.cathode, LED2.cathode, Part1.GND, Part1.N$32, Part1.N$67, U1.GND
  N5: LED1.anode, Part1.N$77
  N6: LED2.anode, Part1.N$177
  3.3V: Part1.3.3V, U1.VCC
  N7: Part1.TX, U1.pin2
  N8: Part1.RX3, U1.pin3
  N9: Part1.N$43, U1.pin4
  N10: Part1.5#97, U1.pin5
  N11: Part1.RSSI, U1.pin6
  N12: Part1.7#99, U1.pin7
  N13: Part1.8, U1.pin8
  N14: Part1.9#101, U1.pin9
  N15: Part1.N$41, U1.pin11
  N16: Part1.2, U1.pin12
  N17: Part1.XBEE_ON, U1.pin13
  N18: Part1.4, U1.pin14
  N19: Part1.5#107, U1.pin15
  N20: Part1.6, U1.pin16
  N21: Part1.7#109, U1.pin17
  N22: Part1.N$28, U1.pin18
  N23: Part1.9#111, U1.pin19
  N24: Part1.10, U1.pin20
